# Fritzing sketch dactylize2 (saved by Fritzing 0.9.2b)
breadboards: 1

parts:
  U1 = 74HC165 [part_number=SN74LS165 package="DIP16 [THT]"]
  U2 = 74HC165 [part_number=SN74LS165 package="DIP16 [THT]"]
  U3 = 74HC165 [part_number=SN74LS165 package="DIP16 [THT]"]
  U4 = 74HC165 [part_number=SN74LS165 package="DIP16 [THT]"]
  U5 = 74HC165 [part_number=SN74LS165 package="DIP16 [THT]"]
  U6 = 74HC165 [part_number=SN74LS165 package="DIP16 [THT]"]
  J2 = double row male pin header, 4 pins [form="♂ (male)"]
  J3 = double row male pin header, 4 pins [form="♂ (male)"]
  J4 = double row male pin header, 4 pins [form="♂ (male)"]
  J5 = double row male pin header, 4 pins [form="♂ (male)"]
  J6 = double row male pin header, 4 pins [form="♂ (male)"]
  J7 = double row male pin header, 4 pins [form="♂ (male)"]
  J8 = double row male pin header, 4 pins [form="♂ (male)"]
  J9 = double row male pin header, 4 pins [form="♂ (male)"]
  J10 = double row male pin header, 4 pins [form="♂ (male)"]
  J11 = double row male pin header, 4 pins [form="♂ (male)"]
  J12 = double row male pin header, 4 pins [form="♂ (male)"]
  Part1 = Arduino Uno (Rev3)
  J13 = double row male pin header, 4 pins [form="♂ (male)"]
  R1 = Resistor [tolerance=±5% resistance=10k package=THT]
  C1 = Ceramic Capacitor [capacitance=100nF package="100 mil [THT, multilayer]"]
  C2 = Ceramic Capacitor [capacitance=100nF package="100 mil [THT, multilayer]"]
  D1 = Rectifier Diode [part_number=1N4001 package="300 mil [THT]"]  # not connected
  R2 = Resistor [tolerance=±5% resistance=10k package=THT]
  R3 = Resistor [tolerance=±5% resistance=10k package=THT]
  R4 = Resistor [tolerance=±5% resistance=10k package=THT]
  R5 = Resistor [tolerance=±5% resistance=10k package=THT]  # not connected
  R6 = Resistor [tolerance=±5% resistance=10k package=THT]
  R7 = Resistor [tolerance=±5% resistance=10k package=THT]
  R9 = Resistor [tolerance=±5% resistance=10k package=THT]
  R10 = Resistor [tolerance=±5% resistance=10k package=THT]
  R11 = Resistor [tolerance=±5% resistance=10k package=THT]
  R12 = Resistor [tolerance=±5% resistance=10k package=THT]
  R13 = Resistor [tolerance=±5% resistance=10k package=THT]
  R14 = Resistor [tolerance=±5% resistance=10k package=THT]
  R15 = Resistor [tolerance=±5% resistance=10k package=THT]
  R16 = Resistor [tolerance=±5% resistance=10k package=THT]
  R17 = Resistor [tolerance=±5% resistance=10k package=THT]
  R18 = Resistor [tolerance=±5% resistance=10k package=THT]
  R19 = Resistor [tolerance=±5% resistance=10k package=THT]
  R20 = Resistor [tolerance=±5% resistance=10k package=THT]
  R21 = Resistor [tolerance=±5% resistance=10k package=THT]
  R22 = Resistor [tolerance=±5% resistance=10k package=THT]
  R23 = Resistor [tolerance=±5% resistance=10k package=THT]
  R24 = Resistor [tolerance=±5% resistance=10k package=THT]
  R25 = Resistor [tolerance=±5% resistance=10k package=THT]
  R26 = Resistor [tolerance=±5% resistance=10k package=THT]
  R27 = Resistor [tolerance=±5% resistance=10k package=THT]
  R28 = Resistor [tolerance=±5% resistance=10k package=THT]
  R29 = Resistor [tolerance=±5% resistance=10k package=THT]
  R30 = Resistor [tolerance=±5% resistance=10k package=THT]
  C3 = Ceramic Capacitor [capacitance=100nF package="100 mil [THT, multilayer]"]
  C4 = Ceramic Capacitor [capacitance=100nF package="100 mil [THT, multilayer]"]
  C5 = Ceramic Capacitor [capacitance=100nF package="100 mil [THT, multilayer]"]
  R31 = Resistor [tolerance=±5% resistance=10k package=THT]
  R32 = Resistor [tolerance=±5% resistance=10k package=THT]
  R33 = Resistor [tolerance=±5% resistance=10k package=THT]
  R34 = Resistor [tolerance=±5% resistance=10k package=THT]
  R35 = Resistor [tolerance=±5% resistance=10k package=THT]
  R36 = Resistor [tolerance=±5% resistance=10k package=THT]
  R37 = Resistor [tolerance=±5% resistance=10k package=THT]
  R38 = Resistor [tolerance=±5% resistance=10k package=THT]
  R39 = Resistor [tolerance=±5% resistance=10k package=THT]
  R40 = Resistor [tolerance=±5% resistance=10k package=THT]
  R41 = Resistor [tolerance=±5% resistance=10k package=THT]
  R42 = Resistor [tolerance=±5% resistance=10k package=THT]
  R43 = Resistor [tolerance=±5% resistance=10k package=THT]
  R44 = Resistor [tolerance=±5% resistance=10k package=THT]
  R45 = Resistor [tolerance=±5% resistance=10k package=THT]
  R46 = Resistor [tolerance=±5% resistance=10k package=THT]
  R47 = Resistor [tolerance=±5% resistance=10k package=THT]
  R48 = Resistor [tolerance=±5% resistance=10k package=THT]
  R49 = Resistor [tolerance=±5% resistance=10k package=THT]
  R50 = Resistor [tolerance=±5% resistance=10k package=THT]
  R51 = Resistor [tolerance=±5% resistance=10k package=THT]
  R52 = Resistor [tolerance=±5% resistance=10k package=THT]  # not connected
  R53 = Resistor [tolerance=±5% resistance=10k package=THT]
  R54 = Resistor [tolerance=±5% resistance=10k package=THT]
  R55 = Resistor [tolerance=±5% resistance=10k package=THT]
  R56 = Resistor [tolerance=±5% resistance=10k package=THT]
  R57 = Resistor [tolerance=±5% resistance=10k package=THT]
  R58 = Resistor [tolerance=±5% resistance=10k package=THT]  # not connected
  R59 = Resistor [tolerance=±5% resistance=10k package=THT]  # not connected
  C6 = Ceramic Capacitor [capacitance=100nF package="100 mil [THT, multilayer]"]  # not connected
  C7 = Ceramic Capacitor [capacitance=100nF package="100 mil [THT, multilayer]"]

nets:
  N1: U1.Q1, U2.Q1, U3.Q1, U4.Q1, Part1.D9_PWM
  N2: U1.Q2, U2.Q2, U3.Q2, U4.Q2, U5.Q1, U5.Q2, U6.Q1, U6.Q2, Part1.D13/SCK
  N3: U1.Q3, J13.pin1, R2.Pin_0
  N4: U1.Q4, J13.pin2, R9.Pin_0
  N5: U1.Q5, J13.pin3, R10.Pin_0
  N6: U1.Q6, J13.pin4, R11.Pin_0
  N7: U1.Q7', Part1.D12/MISO
  N8: U1.MR, U2.Q7'
  N9: U1.SH_CP, J2.pin4, R12.Pin_1
  N10: U1.ST_CP, J2.pin3, R4.Pin_1
  N11: U1.OE, J2.pin2, R3.Pin_1
  N12: U1.DS, J2.pin1, R1.Pin_1
  N13: U1.Q0, U2.Q0, U3.Q0, U4.Q0, U5.Q0, U6.Q0, R6.Pin_1, R7.Pin_1, R25.Pin_1, R31.Pin_1, R45.Pin_1, R53.Pin_1
  N14: U2.Q3, J3.pin1, R16.Pin_0
  N15: U2.Q4, J3.pin2, R17.Pin_0
  N16: U2.Q5, J3.pin3, R18.Pin_0
  N17: U2.Q6, J3.pin4, R19.Pin_0
  N18: U2.MR, U3.Q7'
  N19: U2.SH_CP, J4.pin4, R15.Pin_1
  N20: U2.ST_CP, J4.pin3, R14.Pin_1
  N21: U2.OE, J4.pin2, R13.Pin_1
  N22: U2.DS, J4.pin1, R21.Pin_1
  N23: U3.Q3, J5.pin1, R20.Pin_0
  N24: U3.Q4, J5.pin2, R22.Pin_0
  N25: U3.Q5, J5.pin3, R23.Pin_0
  N26: U3.Q6, J5.pin4, R24.Pin_0
  N27: U3.MR, U4.Q7'
  N28: U3.SH_CP, J6.pin4, R29.Pin_1
  N29: U3.ST_CP, J6.pin3, R28.Pin_1
  N30: U3.OE, J6.pin2, R27.Pin_1
  N31: U3.DS, J6.pin1, R26.Pin_1
  N32: U4.Q3, J7.pin1, R35.Pin_0
  N33: U4.Q4, J7.pin2, R36.Pin_0
  N34: U4.Q5, J7.pin3, R37.Pin_0
  N35: U4.Q6, J7.pin4, R38.Pin_0
  N36: U4.MR, U5.Q7'
  N37: U4.SH_CP, J8.pin4, R30.Pin_1
  N38: U4.ST_CP, J8.pin3, R34.Pin_1
  N39: U4.OE, J8.pin2, R33.Pin_1
  N40: U4.DS, J8.pin1, R32.Pin_1
  N41: U5.Q3, J9.pin1, R41.Pin_0
  N42: U5.Q4, J9.pin2, R42.Pin_0
  N43: U5.Q5, J9.pin3, R43.Pin_0
  N44: U5.Q6, J9.pin4, R44.Pin_0
  N45: U5.MR, U6.Q7'
  N46: U5.SH_CP, J10.pin4, R48.Pin_1
  N47: U5.ST_CP, J10.pin3, R47.Pin_1
  N48: U5.OE, J10.pin2, R46.Pin_1
  N49: U5.DS, J10.pin1, R39.Pin_1
  N50: U6.Q3, J12.pin1, R49.Pin_0
  N51: U6.Q4, J12.pin2, R50.Pin_0
  N52: U6.Q5, J12.pin3, R40.Pin_0
  N53: U6.Q6, J12.pin4, R51.Pin_0
  N54: U6.SH_CP, J11.pin4, R57.Pin_1
  N55: U6.ST_CP, J11.pin3, R56.Pin_1
  N56: U6.OE, J11.pin2, R55.Pin_1
  N57: U6.DS, J11.pin1, R54.Pin_1
  N58: Part1.GND, R2.Pin_1, R9.Pin_1, R10.Pin_1, R11.Pin_1, R16.Pin_1, R17.Pin_1, R18.Pin_1, R19.Pin_1, R20.Pin_1, R22.Pin_1, R23.Pin_1, R24.Pin_1, R35.Pin_1, R36.Pin_1, R37.Pin_1, R38.Pin_1, R40.Pin_1, R41.Pin_1, R42.Pin_1, R43.Pin_1, R44.Pin_1, R49.Pin_1, R50.Pin_1, R51.Pin_1
  N59: R1.Pin_0, C1.1, C2.1, R3.Pin_0, R4.Pin_0, R6.Pin_0, R7.Pin_0, R12.Pin_0, R13.Pin_0, R14.Pin_0, R15.Pin_0, R21.Pin_0, R25.Pin_0, R26.Pin_0, R27.Pin_0, R28.Pin_0, R29.Pin_0, R30.Pin_0, C3.1, C4.1, C5.1, R31.Pin_0, R32.Pin_0, R33.Pin_0, R34.Pin_0, R39.Pin_0, R45.Pin_0, R46.Pin_0, R47.Pin_0, R48.Pin_0, R53.Pin_0, R54.Pin_0, R55.Pin_0, R56.Pin_0, R57.Pin_0, C7.1
  N60: C1.0, C2.0, C3.0, C4.0, C5.0, C7.0

custom parts:
  74HC165: 8-bit parallel-load shift registers
